// Logisim project cpu.circ as structural Verilog: 14 circuits, main circuit cpu
module cpu (
);

  wire CLK, controller_1_out_9, npc_1_en, RST;
  wire [1:0] controller_1_id;
  wire [2:0] controller_1_out_5;
  wire [4:0] controller_1_instruction, controller_1_we, decoder_1_rd, decoder_1_rs, decoder_1_rt,
       decoder_1_shamt, ex_mem_1_out_10, id_ex_1_out_13, mem_wb_1_out_9, multiplexer_2_out,
       multiplexer_3_out, registerfile_1_p6;
  wire [5:0] controller_1_mem, decoder_1_funct, decoder_1_op, ex_mem_1_out_11, id_ex_1_out_14;
  wire [6:0] controller_1_ex, id_ex_1_out_15;
  wire [9:0] divider_1_out_2;
  wire [15:0] decoder_1_imm, \总周期数 , \无条件分支指令数 , \有条件分支成功跳转 , \有条件分支指令数 ;
  wire [23:0] divider1_1_out_2;
  wire [25:0] decoder_1_label;
  wire [31:0] alu_1_result, ex_mem_1_out_9, ex_mem_1_out_12, ex_mem_1_out_13, extender_1_out_3,
       extender_1_out_4, id_ex_1_out_12, id_ex_1_out_16, id_ex_1_out_17, id_ex_1_out_18, id_ex_1_out_19,
       if_id_1_out_6, if_id_1_out_7, mem_wb_1_out_8, mem_wb_1_out_10, mem_wb_1_out_11, mips_ram_1_p8,
       multiplexer_1_out, multiplexer_5_out, multiplexer_6_out, npc_1_new_pc, npc_1_pc4, PC_q,
       registerfile_1_p7, registerfile_1_p8, rom_1_data, SyscallOut;

  Clock clock_1 (.out(CLK));
  Button \u_总复位  (.out(RST));
  Register #(.width(32)) PC (.D(npc_1_new_pc), .en(npc_1_en), .Q(PC_q), .clk(CLK), .clr(RST));
  SumPeriod sumperiod_1 (.in_1(npc_1_en), .in_2(CLK), .out_4(\总周期数 ), .in_3(RST));
  NPC npc_1 (
    .PC_input(PC_q), .new_PC(npc_1_new_pc), .label(decoder_1_label), .IMM(decoder_1_imm),
    .RF1(registerfile_1_p7), .pc_control(controller_1_out_5), .PC4(npc_1_pc4), .RF2(registerfile_1_p8),
    .rst(RST), .clk(CLK), .\成功Cnt (\有条件分支成功跳转 ), .syscall(controller_1_out_9), .en(npc_1_en),
    .oldPC(if_id_1_out_6));
  Hex_Digit_Display hex_digit_display_1 (.value(SyscallOut[27:24]));  // open: dp
  Hex_Digit_Display hex_digit_display_2 (.value(SyscallOut[31:28]));  // open: dp
  Divider divider_1 (.in_1(PC_q), .out_2(divider_1_out_2));
  Hex_Digit_Display hex_digit_display_3 (.value(SyscallOut[23:20]));  // open: dp
  Hex_Digit_Display hex_digit_display_4 (.value(SyscallOut[19:16]));  // open: dp
  Hex_Digit_Display hex_digit_display_5 (.value(SyscallOut[11:8]));  // open: dp
  Hex_Digit_Display hex_digit_display_6 (.value(SyscallOut[15:12]));  // open: dp
  Hex_Digit_Display hex_digit_display_7 (.value(SyscallOut[7:4]));  // open: dp
  Hex_Digit_Display hex_digit_display_8 (.value(SyscallOut[3:0]));  // open: dp
  // Probe on rom_1_data
  ROM #(.addrWidth(10), .dataWidth(32)) rom_1 (.addr(divider_1_out_2), .data(rom_1_data));  // open: sel
  IF_ID if_id_1 (
    .in_1(npc_1_pc4), .in_2(rom_1_data), .\传输状态In (1'b1), .CLK(CLK), .out_6(if_id_1_out_6),
    .out_7(if_id_1_out_7), .\同步清零 (RST));  // open: 传输状态Out
  // Probe on \总周期数 
  // Probe on \无条件分支指令数 
  // Probe on \有条件分支指令数 
  // Probe on \有条件分支成功跳转 
  // Probe on if_id_1_out_7
  Controller controller_1 (
    .op(decoder_1_op), .funct(decoder_1_funct), .out_5(controller_1_out_5), .clk(CLK), .rst(RST),
    .\有条件Cnt (\有条件分支指令数 ), .\无条件Cnt (\无条件分支指令数 ), .ex(controller_1_ex), .ID(controller_1_id),
    .out_9(controller_1_out_9), .mem(controller_1_mem), .WE(controller_1_we),
    .instruction(controller_1_instruction));
  // Probe on mem_wb_1_out_11
  Decoder decoder_1 (
    .shamt(decoder_1_shamt), .op(decoder_1_op), .rs(decoder_1_rs), .label(decoder_1_label),
    .instruction(if_id_1_out_7), .rt(decoder_1_rt), .funct(decoder_1_funct), .rd(decoder_1_rd),
    .IMM(decoder_1_imm));
  Multiplexer #(.select(2), .width(32), .disabled(0), .enable("false")) multiplexer_1 (
    .in0(mem_wb_1_out_11), .in1(mem_wb_1_out_8), .in2(mem_wb_1_out_10), .out(multiplexer_1_out),
    .sel(mem_wb_1_out_9[3:2]));  // open: in3
  Multiplexer #(.select(2), .width(5), .disabled(0), .enable("false")) multiplexer_2 (
    .in0(decoder_1_rd), .in1(decoder_1_rt), .in2({5{1'b1}}), .out(multiplexer_2_out),
    .sel(mem_wb_1_out_9[1:0]));  // open: in3
  Multiplexer #(.width(5), .disabled(0), .enable("false")) multiplexer_3 (
    .in0(decoder_1_rs), .in1(5'b00010), .out(multiplexer_3_out), .sel(controller_1_id[0]));
  // RegisterFile registerfile_1: pin names not known; wires that end beside it: multiplexer_1_out, CLK, mem_wb_1_out_9[4], multiplexer_2_out, multiplexer_3_out, registerfile_1_p6, registerfile_1_p7, registerfile_1_p8, controller_1_instruction, {decoder_1_rt, decoder_1_rd}
  Multiplexer #(.width(5), .disabled(0), .enable("false")) multiplexer_4 (
    .in0(decoder_1_rt), .in1(5'b00100), .out(registerfile_1_p6), .sel(controller_1_id[1]));
  Extender extender_1 (
    .in_1(decoder_1_shamt), .out_3(extender_1_out_3), .out_4(extender_1_out_4), .in_2(decoder_1_imm));
  ID_EX id_ex_1 (
    .in_2(controller_1_we), .in_3(controller_1_mem), .in_4(controller_1_ex), .in_5(registerfile_1_p7),
    .in_6(registerfile_1_p8), .in_7(extender_1_out_3), .in_8(extender_1_out_4), .\传输状态In (1'b1), .CLK(CLK),
    .out_13(id_ex_1_out_13), .out_14(id_ex_1_out_14), .out_15(id_ex_1_out_15), .out_16(id_ex_1_out_16),
    .out_17(id_ex_1_out_17), .out_18(id_ex_1_out_18), .out_19(id_ex_1_out_19), .\同步清零 (RST),
    .in_1(if_id_1_out_6), .out_12(id_ex_1_out_12));  // open: 传输状态Out
  Syscall1 syscall1_1 (.en(id_ex_1_out_15[6]), .cnt(SyscallOut), .clk(CLK), .rst(RST), .a0(id_ex_1_out_17));
  Multiplexer #(.width(32), .disabled(0), .enable("false")) multiplexer_5 (
    .in0(id_ex_1_out_16), .in1(id_ex_1_out_18), .out(multiplexer_5_out), .sel(id_ex_1_out_15[0]));
  ALU alu_1 (.AluOP(id_ex_1_out_15[5:2]), .X(multiplexer_5_out), .Result(alu_1_result), .Y(multiplexer_6_out));
  Multiplexer #(.width(32), .disabled(0), .enable("false")) multiplexer_6 (
    .in0(id_ex_1_out_17), .in1(id_ex_1_out_19), .out(multiplexer_6_out), .sel(id_ex_1_out_15[1]));
  EX_MEM ex_mem_1 (
    .in_2(id_ex_1_out_13), .in_3(id_ex_1_out_14), .in_4(alu_1_result), .in_5(id_ex_1_out_17),
    .\传输状态In (1'b1), .CLK(CLK), .out_10(ex_mem_1_out_10), .out_11(ex_mem_1_out_11), .out_12(ex_mem_1_out_12),
    .out_13(ex_mem_1_out_13), .\同步清零 (RST), .in_1(id_ex_1_out_12), .out_9(ex_mem_1_out_9));  // open: 传输状态Out
  Divider1 divider1_1 (.in_1(ex_mem_1_out_12), .out_2(divider1_1_out_2));
  // MIPS_RAM mips_ram_1: pin names not known; wires that end beside it: divider1_1_out_2, ex_mem_1_out_13, ex_mem_1_out_11[1], ex_mem_1_out_11[5:2], CLK, ex_mem_1_out_11[0], RST, mips_ram_1_p8
  MEM_WB mem_wb_1 (
    .in_2(ex_mem_1_out_10), .\传输状态In (1'b1), .CLK(CLK), .out_9(mem_wb_1_out_9), .\同步清零 (RST),
    .in_4(ex_mem_1_out_12), .out_11(mem_wb_1_out_11), .in_3(mips_ram_1_p8), .out_10(mem_wb_1_out_10),
    .in_1(ex_mem_1_out_9), .out_8(mem_wb_1_out_8));  // open: 传输状态Out

  // Notes on the sheet:
  //   数码管输出应该用寄存器锁存，否则显示数据只能一闪而过
  //   可以通过项目增加Logisim库的方式将前几次实验完成的电路作为子电路引入到本电路中使用
  //   数码管输出
  //   contents of rom_1 (hex, n*v repeats v):
  //   20100000 20110000 20120000 20130000 36100000 36310001 36520002 36730003 ae100000 ae110004 ae120008
  //   ae13000c 2002000a 20110000 20120000 20130000 c
  //   总复位信号应将除ROM以外所有存储组件全部清零
  //   alu
  //   pc4
  //   load
endmodule

module Controller (
  input  [5:0] op,
  input  [5:0] funct,
  input  clk,
  input  rst,
  output [2:0] out_5,
  output [15:0] \有条件Cnt ,
  output [4:0] instruction,
  output [15:0] \无条件Cnt ,
  output out_9,
  output [6:0] ex,
  output [5:0] mem,
  output [4:0] WE,
  output [1:0] ID
);

  wire add, addi, addiu, adds, addu, \and , andi, ands, beq, bltz, bne, cmps, comparator_1_eq,
       comparator_16_eq, comparator_17_eq, comparator_18_eq, comparator_19_eq, comparator_20_eq,
       comparator_21_eq, comparator_22_eq, comparator_23_eq, comparator_24_eq, comparator_25_eq,
       comparator_26_eq, comparator_27_eq, comparator_28_eq, comparator_29_eq, j, jal, jr, js, \nor , \or ,
       or_2_out, or_9_out, or_11_out, or_12_out, ori, ors, rlshifters, sb, sll, slt, slti, sltu, sra, srl,
       srlv, sub, sw, xori;

  Comparator #(.width(6)) comparator_1 (.a(op), .b({6{1'b0}}), .eq(comparator_1_eq));  // open: gt, lt
  Comparator #(.width(6)) comparator_2 (.a(op), .b(6'b001000), .eq(addi));  // open: gt, lt
  Comparator #(.width(6)) comparator_3 (.a(op), .b(6'b001001), .eq(addiu));  // open: gt, lt
  Comparator #(.width(6)) comparator_4 (.a(op), .b(6'b001100), .eq(andi));  // open: gt, lt
  Comparator #(.width(6)) comparator_5 (.a(op), .b(6'b001101), .eq(ori));  // open: gt, lt
  Comparator #(.width(6)) comparator_6 (.a(op), .b(6'b001110), .eq(xori));  // open: gt, lt
  Comparator #(.width(6)) comparator_7 (.a(op), .b(6'b001010), .eq(slti));  // open: gt, lt
  Comparator #(.width(6)) comparator_8 (.a(op), .b(6'b100011), .eq(mem[0]));  // open: gt, lt
  Comparator #(.width(6)) comparator_9 (.a(op), .b(6'b101011), .eq(sw));  // open: gt, lt
  Comparator #(.width(6)) comparator_10 (.a(op), .b(6'b101000), .eq(sb));  // open: gt, lt
  Comparator #(.width(6)) comparator_11 (.a(op), .b(6'b000100), .eq(beq));  // open: gt, lt
  Comparator #(.width(6)) comparator_12 (.a(op), .b(6'b000101), .eq(bne));  // open: gt, lt
  Comparator #(.width(6)) comparator_13 (.a(op), .b(6'b000001), .eq(bltz));  // open: gt, lt
  Comparator #(.width(6)) comparator_14 (.a(op), .b(6'b000010), .eq(j));  // open: gt, lt
  Comparator #(.width(6)) comparator_15 (.a(op), .b(6'b000011), .eq(jal));  // open: gt, lt
  Comparator #(.width(6)) comparator_16 (.a(funct), .b(6'b100000), .eq(comparator_16_eq));  // open: gt, lt
  Comparator #(.width(6)) comparator_17 (.a(funct), .b(6'b100001), .eq(comparator_17_eq));  // open: gt, lt
  Comparator #(.width(6)) comparator_18 (.a(funct), .b(6'b100100), .eq(comparator_18_eq));  // open: gt, lt
  Comparator #(.width(6)) comparator_19 (.a(funct), .b(6'b100010), .eq(comparator_19_eq));  // open: gt, lt
  Comparator #(.width(6)) comparator_20 (.a(funct), .b(6'b100101), .eq(comparator_20_eq));  // open: gt, lt
  Comparator #(.width(6)) comparator_21 (.a(funct), .b(6'b100111), .eq(comparator_21_eq));  // open: gt, lt
  Comparator #(.width(6)) comparator_22 (.a(funct), .b(6'b000110), .eq(comparator_22_eq));  // open: gt, lt
  Comparator #(.width(6)) comparator_23 (.a(funct), .b(6'b101010), .eq(comparator_23_eq));  // open: gt, lt
  Comparator #(.width(6)) comparator_24 (.a(funct), .b(6'b101011), .eq(comparator_24_eq));  // open: gt, lt
  Comparator #(.width(6)) comparator_25 (.a(funct), .b({6{1'b0}}), .eq(comparator_25_eq));  // open: gt, lt
  Comparator #(.width(6)) comparator_26 (.a(funct), .b(6'b000011), .eq(comparator_26_eq));  // open: gt, lt
  Comparator #(.width(6)) comparator_27 (.a(funct), .b(6'b000010), .eq(comparator_27_eq));  // open: gt, lt
  Comparator #(.width(6)) comparator_28 (.a(funct), .b(6'b001000), .eq(comparator_28_eq));  // open: gt, lt
  Comparator #(.width(6)) comparator_29 (.a(funct), .b(6'b001100), .eq(comparator_29_eq));  // open: gt, lt
  and and_1 (add, comparator_1_eq, comparator_16_eq);
  and and_2 (addu, comparator_1_eq, comparator_17_eq);
  and and_3 (\and , comparator_1_eq, comparator_18_eq);
  and and_4 (sub, comparator_1_eq, comparator_19_eq);
  and and_5 (\or , comparator_1_eq, comparator_20_eq);
  and and_6 (\nor , comparator_1_eq, comparator_21_eq);
  and and_7 (srlv, comparator_1_eq, comparator_22_eq);
  and and_8 (slt, comparator_1_eq, comparator_23_eq);
  and and_9 (sltu, comparator_1_eq, comparator_24_eq);
  and and_10 (sll, comparator_1_eq, comparator_25_eq);
  and and_11 (sra, comparator_1_eq, comparator_26_eq);
  and and_12 (srl, comparator_1_eq, comparator_27_eq);
  and and_13 (jr, comparator_1_eq, comparator_28_eq);
  and and_14 (ex[6], comparator_1_eq, comparator_29_eq);
  Priority_Encoder #(.select(5)) priority_encoder_1 (
    .in0(addi), .in1(addiu), .in2(andi), .in3(ori), .in4(xori), .in5(slti), .in6(mem[0]), .in7(sw), .in8(sb),
    .in9(beq), .in10(bne), .in11(bltz), .in12(j), .in13(jal), .in14(add), .in15(addu), .in16(\and ),
    .in17(sub), .in18(\or ), .in19(\nor ), .in20(srlv), .in21(slt), .in22(sltu), .in23(sll), .in24(sra),
    .in25(srl), .in26(jr), .in27(ex[6]), .in28(1'b0), .in29(1'b0), .in30(1'b0), .in31(1'b0), .out(instruction));  // open: gs, en_out, en_in
  or or_1 (ex[0], sll, sra, srl);
  or or_2 (or_2_out, addi, addiu, andi, ori, xori, slti, mem[0], sw, sb);
  or or_3 (cmps, slti, bltz, slt);
  or or_4 (ors, \or , ori);
  or or_5 (ands, \and , andi);
  or or_6 (rlshifters, srlv, srl);
  Priority_Encoder #(.select(1)) priority_encoder_2 (
    .in0(1'b1), .in1(or_2_out), .out(ex[1]));  // open: gs, en_out, en_in
  or or_7 (adds, mem[0], add, addi, sb, addu, addiu, sw);
  Priority_Encoder #(.select(4)) priority_encoder_3 (
    .in0(1'b1), .in1(sra), .in2(rlshifters), .in3(1'b0), .in4(1'b0), .in5(adds), .in6(sub), .in7(ands),
    .in8(ors), .in9(xori), .in10(\nor ), .in11(cmps), .in12(sltu), .in13(1'b0), .in14(1'b0), .in15(1'b0),
    .out(ex[5:2]));  // open: gs, en_out, en_in
  not not_1 (mem[5], sb);
  or or_8 (mem[1], sw, sb);
  Priority_Encoder #(.select(1)) priority_encoder_4 (.in0(1'b1), .in1(ex[6]), .out(ID[1]));  // open: gs, en_out, en_in
  or or_9 (or_9_out, addi, addiu, andi, ori, xori, slti, mem[0]);
  Priority_Encoder #(.select(2)) priority_encoder_5 (
    .in0(1'b1), .in1(jal), .in2(mem[0]), .in3(1'b0), .out(WE[3:2]));  // open: gs, en_out, en_in
  nor nor_1 (WE[4], sw, sb, beq, bne, bltz, j, jr, ex[6]);
  Priority_Encoder #(.select(2)) priority_encoder_6 (
    .in0(1'b1), .in1(or_9_out), .in2(jal), .in3(1'b0), .out(WE[1:0]));  // open: gs, en_out, en_in
  or or_10 (js, j, jal);
  Priority_Encoder priority_encoder_7 (
    .in0(1'b1), .in1(beq), .in2(bne), .in3(bltz), .in4(js), .in5(jr), .in6(1'b0), .in7(1'b0), .out(out_5));  // open: en_in, gs, en_out
  Counter #(.width(16), .max('hffff)) counter_1 (
    .count(or_11_out), .Q(\有条件Cnt ), .clk(clk), .clr(rst));  // open: load, D, carry
  or or_11 (or_11_out, bltz, bne, beq);
  Counter #(.width(16), .max('hffff)) counter_2 (
    .count(or_12_out), .Q(\无条件Cnt ), .clk(clk), .clr(rst));  // open: load, D, carry
  or or_12 (or_12_out, j, jal, jr);
  not not_2 (out_9, ex[6]);

  assign ID[0] = ID[1];
  assign mem[4:2] = {{2{mem[5]}}, 1'b1};

  // Other names for the same wires on the sheet: CPC[2:0] = out_5; CA = ex[0]; CB = ex[1]; ALUop[3:0] = ex[5:2];
  //   SysC1 = ex[6]; syscall = ex[6]; Ra = ID[1]; Rb = ID[1]; ld = mem[0]; lw = mem[0]; str = mem[1];
  //   Sel[3:1] = {3{mem[5]}}; SysC2 = out_9; Rw[1:0] = WE[1:0]; Din[1:0] = WE[3:2]; We_t = WE[4];
  //   无条件[15:0] = \无条件Cnt ; 有条件[15:0] = \有条件Cnt 
endmodule

module NPC (
  input  [15:0] IMM,
  input  [31:0] PC_input,
  input  [31:0] oldPC,
  input  syscall,
  input  [31:0] RF1,
  input  [2:0] pc_control,
  input  clk,
  input  rst,
  input  [25:0] label,
  input  [31:0] RF2,
  output [31:0] new_PC,
  output en,
  output [31:0] PC4,
  output [15:0] \成功Cnt 
);

  wire and_2_out, and_3_out, and_4_out, comparator_1_eq, comparator_2_eq, comparator_3_lt, comparator_4_eq,
       comparator_5_eq, comparator_6_eq, not_1_out, or_3_out;
  wire [31:0] and_1_out, bit_extender_1_out, bit_extender_2_out, Cbeq, Cbltz, Cbne, PC4offset, PCLabel;

  Adder #(.width(32)) adder_1 (.a(PC_input), .b(32'h4), .out(PC4));  // open: cin, cout
  Comparator #(.width(32)) comparator_1 (.a(RF1), .b(32'h22), .eq(comparator_1_eq));  // open: gt, lt
  assign bit_extender_1_out = {{14{IMM[15]}}, {IMM, 2'b00}};  // Bit_Extender bit_extender_1
  assign and_1_out = PC_input & 32'hf0000000;  // AND_Gate and_1, 32 bits wide
  assign bit_extender_2_out = {{4{1'b0}}, {label, 2'b00}};  // Bit_Extender bit_extender_2
  Adder #(.width(32)) adder_2 (.a(bit_extender_1_out), .b(oldPC), .out(PC4offset));  // open: cin, cout
  assign PCLabel = and_1_out | bit_extender_2_out;  // OR_Gate or_1, 32 bits wide
  or or_2 (en, comparator_1_eq, syscall);
  Comparator #(.width(32)) comparator_2 (.a(RF1), .b(RF2), .eq(comparator_2_eq));  // open: gt, lt
  Comparator #(.width(32)) comparator_3 (.a(RF1), .b(RF2), .lt(comparator_3_lt));  // open: gt, eq
  Multiplexer #(.width(32), .disabled(0), .enable("false")) multiplexer_1 (
    .in0(oldPC), .in1(PC4offset), .out(Cbeq), .sel(comparator_2_eq));
  Multiplexer #(.width(32), .disabled(0), .enable("false")) multiplexer_2 (
    .in0(PC4offset), .in1(oldPC), .out(Cbne), .sel(comparator_2_eq));
  Comparator #(.width(3)) comparator_4 (.a(pc_control), .b(3'b001), .eq(comparator_4_eq));  // open: gt, lt
  Comparator #(.width(3)) comparator_5 (.a(pc_control), .b(3'b010), .eq(comparator_5_eq));  // open: gt, lt
  not not_1 (not_1_out, comparator_2_eq);
  Comparator #(.width(3)) comparator_6 (.a(pc_control), .b(3'b011), .eq(comparator_6_eq));  // open: gt, lt
  Multiplexer #(.width(32), .disabled(0), .enable("false")) multiplexer_3 (
    .in0(oldPC), .in1(PC4offset), .out(Cbltz), .sel(comparator_3_lt));
  and and_2 (and_2_out, comparator_4_eq, comparator_2_eq);
  and and_3 (and_3_out, comparator_5_eq, not_1_out);
  and and_4 (and_4_out, comparator_6_eq, comparator_3_lt);
  Counter #(.width(16), .max('hffff)) counter_1 (
    .count(or_3_out), .Q(\成功Cnt ), .clk(clk), .clr(rst));  // open: load, D, carry
  or or_3 (or_3_out, and_2_out, and_3_out, and_4_out);
  Multiplexer #(.select(3), .width(32), .disabled(0), .enable("false")) multiplexer_4 (
    .in0(oldPC), .in1(Cbeq), .in2(Cbne), .in3(Cbltz), .in4(PCLabel), .in5(RF1), .in6({32{1'b0}}),
    .in7({32{1'b0}}), .out(new_PC), .sel(pc_control));

  // Other names for the same wires on the sheet: CNPC[2:0] = pc_control; Input[31:0] = PC_input; oldPC4[31:0] = oldPC;
  //   Output[31:0] = new_PC; success[15:0] = \成功Cnt 
endmodule

module Divider (
  input  [31:0] in_1,
  output [9:0] out_2
);


  assign out_2 = in_1[11:2];

  // Other names for the same wires on the sheet: Input[31:0] = in_1; Output[9:0] = in_1[11:2]
endmodule

module Divider1 (
  input  [31:0] in_1,
  output [23:0] out_2
);


  assign out_2 = in_1[25:2];

  // Other names for the same wires on the sheet: Input[31:0] = in_1; Output[23:0] = in_1[25:2]
endmodule

module Decoder (
  input  [31:0] instruction,
  output [4:0] shamt,
  output [5:0] op,
  output [4:0] rs,
  output [25:0] label,
  output [4:0] rt,
  output [5:0] funct,
  output [4:0] rd,
  output [15:0] IMM
);


  assign funct = instruction[5:0];
  assign IMM = instruction[15:0];
  assign label = instruction[25:0];
  assign op = instruction[31:26];
  assign rd = instruction[15:11];
  assign rs = instruction[25:21];
  assign rt = instruction[20:16];
  assign shamt = instruction[10:6];

  // Other names for the same wires on the sheet: Input[31:0] = instruction; s[4:0] = instruction[10:6]
endmodule

module Extender (
  input  [4:0] in_1,
  input  [15:0] in_2,
  output [31:0] out_3,
  output [31:0] out_4
);

  assign out_3 = {{27{in_1[4]}}, in_1};  // Bit_Extender bit_extender_1
  assign out_4 = {{16{in_2[15]}}, in_2};  // Bit_Extender bit_extender_2

  // Other names for the same wires on the sheet: eIMM[31:0] = out_4; es[31:0] = out_3; IMM[15:0] = in_2;
  //   s[4:0] = in_1
endmodule

module Syscall (
  input  in_1,
  input  in_2,
  output out_3
);

  wire not_1_out;

  not not_1 (not_1_out, in_1);
  or or_1 (out_3, not_1_out, in_2);

  // Other names for the same wires on the sheet: enable = out_3; eq = in_1; syscall = in_2
endmodule

module SumPeriod (
  input  in_1,
  input  in_2,
  input  in_3,
  output [15:0] out_4
);

  wire [15:0] adder_1_out, counter_1_q;

  Counter #(.width(16), .max('hffff)) counter_1 (
    .count(in_1), .Q(counter_1_q), .clk(in_2), .clr(in_3));  // open: load, D, carry
  Adder #(.width(16)) adder_1 (.a(16'h1), .b(counter_1_q), .out(adder_1_out));  // open: cin, cout
  Multiplexer #(.width(16), .disabled(0), .enable("false")) multiplexer_1 (
    .in0(adder_1_out), .in1(counter_1_q), .out(out_4), .sel(in_1));

  // Other names for the same wires on the sheet: CLK = in_2; cnt[15:0] = out_4; enable = in_1; RST = in_3
endmodule

module Syscall1 (
  input  en,
  input  clk,
  input  rst,
  input  [31:0] a0,
  output [31:0] cnt
);

  Register #(.width(32)) register_1 (.D(a0), .en(en), .Q(cnt), .clk(clk), .clr(rst));

  // Other names for the same wires on the sheet: enable = en; Input[31:0] = a0; Output[31:0] = cnt
endmodule

module IF_ID (
  input  [31:0] in_1,
  input  [31:0] in_2,
  input  \传输状态In ,
  input  CLK,
  input  \同步清零 ,
  output [31:0] out_6,
  output [31:0] out_7,
  output \传输状态Out 
);

  wire multiplexer_3_out;
  wire [31:0] multiplexer_1_out, multiplexer_2_out;

  Multiplexer #(.width(32), .enable("false")) multiplexer_1 (
    .in0(in_1), .in1({32{1'b0}}), .out(multiplexer_1_out), .sel(\同步清零 ));
  Multiplexer #(.width(32), .enable("false")) multiplexer_2 (
    .in0(in_2), .in1({32{1'b0}}), .out(multiplexer_2_out), .sel(\同步清零 ));
  Multiplexer #(.enable("false")) multiplexer_3 (.in0(\传输状态In ), .in1(1'b0), .out(multiplexer_3_out), .sel(\同步清零 ));
  Register #(.width(32)) register_1 (.D(multiplexer_1_out), .en(\传输状态In ), .Q(out_6), .clk(CLK));  // open: clr
  Register #(.width(32)) register_2 (.D(multiplexer_2_out), .en(\传输状态In ), .Q(out_7), .clk(CLK));  // open: clr
  Register #(.width(1)) register_3 (.D(multiplexer_3_out), .en(\传输状态In ), .Q(\传输状态Out ), .clk(CLK));  // open: clr
endmodule

module ID_EX (
  input  [31:0] in_1,
  input  [4:0] in_2,
  input  [5:0] in_3,
  input  [6:0] in_4,
  input  [31:0] in_5,
  input  [31:0] in_6,
  input  [31:0] in_7,
  input  [31:0] in_8,
  input  \传输状态In ,
  input  CLK,
  input  \同步清零 ,
  output [31:0] out_12,
  output [4:0] out_13,
  output [5:0] out_14,
  output [6:0] out_15,
  output [31:0] out_16,
  output [31:0] out_17,
  output [31:0] out_18,
  output [31:0] out_19,
  output \传输状态Out 
);

  wire multiplexer_9_out;
  wire [4:0] multiplexer_2_out;
  wire [5:0] multiplexer_3_out;
  wire [6:0] multiplexer_4_out;
  wire [31:0] multiplexer_1_out, multiplexer_5_out, multiplexer_6_out, multiplexer_7_out, multiplexer_8_out;

  Multiplexer #(.width(32), .enable("false")) multiplexer_1 (
    .in0(in_1), .in1({32{1'b0}}), .out(multiplexer_1_out), .sel(\同步清零 ));
  Multiplexer #(.width(5), .enable("false")) multiplexer_2 (
    .in0(in_2), .in1({5{1'b0}}), .out(multiplexer_2_out), .sel(\同步清零 ));
  Multiplexer #(.width(6), .enable("false")) multiplexer_3 (
    .in0(in_3), .in1({6{1'b0}}), .out(multiplexer_3_out), .sel(\同步清零 ));
  Multiplexer #(.width(7), .enable("false")) multiplexer_4 (
    .in0(in_4), .in1({7{1'b0}}), .out(multiplexer_4_out), .sel(\同步清零 ));
  Multiplexer #(.width(32), .enable("false")) multiplexer_5 (
    .in0(in_5), .in1({32{1'b0}}), .out(multiplexer_5_out), .sel(\同步清零 ));
  Multiplexer #(.width(32), .enable("false")) multiplexer_6 (
    .in0(in_6), .in1({32{1'b0}}), .out(multiplexer_6_out), .sel(\同步清零 ));
  Multiplexer #(.width(32), .enable("false")) multiplexer_7 (
    .in0(in_7), .in1({32{1'b0}}), .out(multiplexer_7_out), .sel(\同步清零 ));
  Multiplexer #(.width(32), .enable("false")) multiplexer_8 (
    .in0(in_8), .in1({32{1'b0}}), .out(multiplexer_8_out), .sel(\同步清零 ));
  Multiplexer #(.enable("false")) multiplexer_9 (.in0(\传输状态In ), .in1(1'b0), .out(multiplexer_9_out), .sel(\同步清零 ));
  Register #(.width(32)) register_1 (.D(multiplexer_1_out), .en(\传输状态In ), .Q(out_12), .clk(CLK));  // open: clr
  Register #(.width(5)) register_2 (.D(multiplexer_2_out), .en(\传输状态In ), .Q(out_13), .clk(CLK));  // open: clr
  Register #(.width(6)) register_3 (.D(multiplexer_3_out), .en(\传输状态In ), .Q(out_14), .clk(CLK));  // open: clr
  Register #(.width(7)) register_4 (.D(multiplexer_4_out), .en(\传输状态In ), .Q(out_15), .clk(CLK));  // open: clr
  Register #(.width(32)) register_5 (.D(multiplexer_5_out), .en(\传输状态In ), .Q(out_16), .clk(CLK));  // open: clr
  Register #(.width(32)) register_6 (.D(multiplexer_6_out), .en(\传输状态In ), .Q(out_17), .clk(CLK));  // open: clr
  Register #(.width(32)) register_7 (.D(multiplexer_7_out), .en(\传输状态In ), .Q(out_18), .clk(CLK));  // open: clr
  Register #(.width(32)) register_8 (.D(multiplexer_8_out), .en(\传输状态In ), .Q(out_19), .clk(CLK));  // open: clr
  Register #(.width(1)) register_9 (.D(multiplexer_9_out), .en(\传输状态In ), .Q(\传输状态Out ), .clk(CLK));  // open: clr
endmodule

module EX_MEM (
  input  [31:0] in_1,
  input  [4:0] in_2,
  input  [5:0] in_3,
  input  [31:0] in_4,
  input  [31:0] in_5,
  input  \传输状态In ,
  input  CLK,
  input  \同步清零 ,
  output [31:0] out_9,
  output [4:0] out_10,
  output [5:0] out_11,
  output [31:0] out_12,
  output [31:0] out_13,
  output \传输状态Out 
);

  wire multiplexer_6_out;
  wire [4:0] multiplexer_2_out;
  wire [5:0] multiplexer_3_out;
  wire [31:0] multiplexer_1_out, multiplexer_4_out, multiplexer_5_out;

  Multiplexer #(.width(32), .enable("false")) multiplexer_1 (
    .in0(in_1), .in1({32{1'b0}}), .out(multiplexer_1_out), .sel(\同步清零 ));
  Multiplexer #(.width(5), .enable("false")) multiplexer_2 (
    .in0(in_2), .in1({5{1'b0}}), .out(multiplexer_2_out), .sel(\同步清零 ));
  Multiplexer #(.width(6), .enable("false")) multiplexer_3 (
    .in0(in_3), .in1({6{1'b0}}), .out(multiplexer_3_out), .sel(\同步清零 ));
  Multiplexer #(.width(32), .enable("false")) multiplexer_4 (
    .in0(in_4), .in1({32{1'b0}}), .out(multiplexer_4_out), .sel(\同步清零 ));
  Multiplexer #(.width(32), .enable("false")) multiplexer_5 (
    .in0(in_5), .in1({32{1'b0}}), .out(multiplexer_5_out), .sel(\同步清零 ));
  Multiplexer #(.enable("false")) multiplexer_6 (.in0(\传输状态In ), .in1(1'b0), .out(multiplexer_6_out), .sel(\同步清零 ));
  Register #(.width(32)) register_1 (.D(multiplexer_1_out), .en(\传输状态In ), .Q(out_9), .clk(CLK));  // open: clr
  Register #(.width(5)) register_2 (.D(multiplexer_2_out), .en(\传输状态In ), .Q(out_10), .clk(CLK));  // open: clr
  Register #(.width(6)) register_3 (.D(multiplexer_3_out), .en(\传输状态In ), .Q(out_11), .clk(CLK));  // open: clr
  Register #(.width(32)) register_4 (.D(multiplexer_4_out), .en(\传输状态In ), .Q(out_12), .clk(CLK));  // open: clr
  Register #(.width(32)) register_5 (.D(multiplexer_5_out), .en(\传输状态In ), .Q(out_13), .clk(CLK));  // open: clr
  Register #(.width(1)) register_6 (.D(multiplexer_6_out), .en(\传输状态In ), .Q(\传输状态Out ), .clk(CLK));  // open: clr
endmodule

module MEM_WB (
  input  [31:0] in_1,
  input  [4:0] in_2,
  input  [31:0] in_3,
  input  [31:0] in_4,
  input  \传输状态In ,
  input  CLK,
  input  \同步清零 ,
  output [31:0] out_8,
  output [4:0] out_9,
  output [31:0] out_10,
  output [31:0] out_11,
  output \传输状态Out 
);

  wire multiplexer_5_out;
  wire [4:0] multiplexer_2_out;
  wire [31:0] multiplexer_1_out, multiplexer_3_out, multiplexer_4_out;

  Multiplexer #(.width(32), .enable("false")) multiplexer_1 (
    .in0(in_1), .in1({32{1'b0}}), .out(multiplexer_1_out), .sel(\同步清零 ));
  Multiplexer #(.width(5), .enable("false")) multiplexer_2 (
    .in0(in_2), .in1({5{1'b0}}), .out(multiplexer_2_out), .sel(\同步清零 ));
  Multiplexer #(.width(32), .enable("false")) multiplexer_3 (
    .in0(in_3), .in1({32{1'b0}}), .out(multiplexer_3_out), .sel(\同步清零 ));
  Multiplexer #(.width(32), .enable("false")) multiplexer_4 (
    .in0(in_4), .in1({32{1'b0}}), .out(multiplexer_4_out), .sel(\同步清零 ));
  Multiplexer #(.enable("false")) multiplexer_5 (.in0(\传输状态In ), .in1(1'b0), .out(multiplexer_5_out), .sel(\同步清零 ));
  Register #(.width(32)) register_1 (.D(multiplexer_1_out), .en(\传输状态In ), .Q(out_8), .clk(CLK));  // open: clr
  Register #(.width(5)) register_2 (.D(multiplexer_2_out), .en(\传输状态In ), .Q(out_9), .clk(CLK));  // open: clr
  Register #(.width(32)) register_3 (.D(multiplexer_3_out), .en(\传输状态In ), .Q(out_10), .clk(CLK));  // open: clr
  Register #(.width(32)) register_4 (.D(multiplexer_4_out), .en(\传输状态In ), .Q(out_11), .clk(CLK));  // open: clr
  Register #(.width(1)) register_5 (.D(multiplexer_5_out), .en(\传输状态In ), .Q(\传输状态Out ), .clk(CLK));  // open: clr
endmodule
